# Fritzing sketch Plan (saved by Fritzing 0.9.0b)
breadboards: 1

parts:
  R1 = Rotary Potentiometer (Small) [maximum_resistance=100kΩ package=THT]
  J1 = Infrared Proximity Sensor
  Bauteil1 = Arduino Leonardo (Rev3b)

nets:
  VCC: R1.leg1, J1.Vcc, Bauteil1.5V
  N1: R1.wiper, Bauteil1.A0
  GND: R1.leg2, J1.GND, Bauteil1.GND
  N2: J1.Vout, Bauteil1.A3
